// Logisim project 28bit_alu.circ as structural Verilog: 11 circuits, main circuit Input_way
module main (
  input  [1:0] in_1,
  input  [27:0] in_2,
  input  [27:0] in_3,
  output [27:0] out_4,
  output zero,
  output negative,
  output overflow,
  output carrry
);

  ALU_broad alu_broad_1 (
    .A(in_2), .B(in_3), .control0(in_1[1]), .control1(in_1[0]), .result(out_4), .zero(zero),
    .negative(negative), .overflow(overflow), .carry(carrry));
endmodule

module Input_way (
  input  [27:0] Input
);
endmodule

module ANDCIRC (
  input  [27:0] in_1,
  input  [27:0] in_2,
  output [27:0] out_3
);

  assign out_3 = in_1 & in_2;  // AND_Gate and_1, 28 bits wide
endmodule

module ORCIRC (
  input  [27:0] in_1,
  input  [27:0] in_2,
  output [27:0] out_3
);

  assign out_3 = in_1 | in_2;  // OR_Gate or_1, 28 bits wide
endmodule

module FULL_adder (
  input  carry_in,
  input  A,
  input  B,
  output out_4,
  output out_5
);

  wire and_1_out, and_2_out, xor_1_out;

  and and_1 (and_1_out, B, A);
  xor xor_1 (xor_1_out, A, B);
  or or_1 (out_5, and_1_out, and_2_out);
  and and_2 (and_2_out, xor_1_out, carry_in);
  xor xor_2 (out_4, carry_in, xor_1_out);
endmodule

module big_full_adder (
  input  in_1,
  input  [27:0] in_2,
  input  [27:0] in_3,
  output [27:0] out_4,
  output out_5
);

  Adder #(.width(28)) adder_1 (.a(in_2), .b(in_3), .out(out_4), .cin(in_1), .cout(out_5));
endmodule

module x_or (
  input  [27:0] in_1,
  input  [27:0] in_2,
  output [27:0] out_3
);

  assign out_3 = in_1 ^ in_2;  // XOR_Gate xor_1, 28 bits wide
endmodule

module add_sub (
  input  in_1,
  input  [27:0] A,
  input  [27:0] B,
  output [27:0] out_4,
  output out_5,
  output out_6
);

  wire and_1_out, and_2_out, msb_get_out_2, msb_gett_out_2, msb_getter_out_2, not_1_out, not_2_out, not_3_out;
  wire [27:0] big_x_or_out_3;

  get_the_msb msb_get (.Input(A), .out_2(msb_get_out_2));
  not not_1 (not_1_out, msb_get_out_2);
  x_or big_x_or (.in_1({28{in_1}}), .in_2(B), .out_3(big_x_or_out_3));
  get_the_msb msb_getter (.Input(B), .out_2(msb_getter_out_2));
  not not_2 (not_2_out, msb_getter_out_2);
  big_full_adder big_full_adder_1 (.in_2(A), .in_3(big_x_or_out_3), .in_1(in_1), .out_5(out_5), .out_4(out_4));
  get_the_msb msb_gett (.Input(out_4), .out_2(msb_gett_out_2));
  not not_3 (not_3_out, msb_gett_out_2);
  and and_1 (and_1_out, not_3_out, msb_getter_out_2, msb_get_out_2);
  and and_2 (and_2_out, msb_gett_out_2, not_2_out, not_1_out);
  or or_1 (out_6, and_1_out, and_2_out);
endmodule

module get_the_msb (
  input  [27:0] Input,
  output out_2
);


  assign out_2 = Input[27];
endmodule

module ALU_broad (
  input  control1,
  input  control0,
  input  [27:0] A,
  input  [27:0] B,
  output [27:0] result,
  output zero,
  output negative,
  output overflow,
  output carry
);

  wire seventeen_bit_reduced_or_1_out_2;
  wire [27:0] add_sub_1_out_4, andcirc_1_out_3, multiplexer_1_out, orcirc_1_out_3;

  ANDCIRC andcirc_1 (.in_1(A), .in_2(B), .out_3(andcirc_1_out_3));
  ORCIRC orcirc_1 (.in_1(A), .in_2(B), .out_3(orcirc_1_out_3));
  add_sub add_sub_1 (.A(A), .B(B), .in_1(control0), .out_4(add_sub_1_out_4), .out_5(carry), .out_6(overflow));
  Multiplexer #(.width(28), .enable("false")) multiplexer_1 (
    .in0(andcirc_1_out_3), .in1(orcirc_1_out_3), .out(multiplexer_1_out), .sel(control0));
  Multiplexer #(.width(28), .enable("false")) multiplexer_2 (
    .in0(multiplexer_1_out), .in1(add_sub_1_out_4), .out(result), .sel(control1));
  get_the_msb get_the_msb_1 (.Input(result), .out_2(negative));
  seventeen_bit_reduced_or seventeen_bit_reduced_or_1 (.in_1(result), .out_2(seventeen_bit_reduced_or_1_out_2));
  not not_1 (zero, seventeen_bit_reduced_or_1_out_2);
endmodule

module seventeen_bit_reduced_or (
  input  [27:0] in_1,
  output out_2
);

  or or_1 (out_2, in_1[0], in_1[1], in_1[2], in_1[3], in_1[4], in_1[5], in_1[6], in_1[7], in_1[8], in_1[9], in_1[10], in_1[11], in_1[12], in_1[13], in_1[14], in_1[15], in_1[16], in_1[17], in_1[18], in_1[19], in_1[20], in_1[21], in_1[22], in_1[23], in_1[24], in_1[25], in_1[26], in_1[27]);
endmodule
