// Logisim project 28bit_cpu.circ as structural Verilog: 3 circuits, main circuit main
module main (
);

  wire clock_1_out, cpu_1_r, cpu_1_w, Reset_out;
  wire [23:0] cpu_1_addr;
  wire [27:0] cpu_1_dataout, ram_1_data;

  Clock clock_1 (.out(clock_1_out));
  Button Reset (.out(Reset_out));
  CPU cpu_1 (
    .Clk(clock_1_out), .Reset(Reset_out), .R(cpu_1_r), .W(cpu_1_w), .Addr(cpu_1_addr), .DataIn(ram_1_data),
    .DataOut(cpu_1_dataout));
  RAM #(.addrWidth(24), .dataWidth(28), .bus("separate")) ram_1 (
    .addr(cpu_1_addr), .din(cpu_1_dataout), .data(ram_1_data), .str(cpu_1_w), .clk(clock_1_out), .ld(cpu_1_r));  // open: sel, clr

  // Notes on the sheet:
  //   9-dec
  //   0 - AND
  //   1 - ADD
  //   2 - STO
  //   3 - OR
  //   4 - SUB
  //   5 - BUN
  //   6 - LDA
  //   7 - HLT
  //   8-inc
endmodule

module CPU (
  input  Clk,
  input  Reset,
  input  [27:0] DataIn,
  output R,
  output W,
  output [23:0] Addr,
  output [27:0] DataOut
);

  wire ac_enable, b1, booth_s_multiplier_1_done, c0, c1, controlunit_1_c1, controlunit_1_c2,
       controlunit_1_decrement_ac, controlunit_1_increment_ac, d1, d2, LdA, LdA_from_MBR, LoadAc, LoadB,
       LoadMAR, mul_load, mul_start, or_1_out;
  wire [23:0] counter_1_q, multiplexer_1_out;
  wire [27:0] Ac, Ac_in_normal, AcIn, ALUout, booth_s_multiplier_1_product_low, multiplexer_3_out,
       multiplexer_4_out;

  Multiplexer #(.width(24), .enable("false")) multiplexer_1 (
    .in0(counter_1_q), .in1(DataOut[23:0]), .out(multiplexer_1_out), .sel(d2));
  Multiplexer #(.width(28), .enable("false")) multiplexer_2 (
    .in0(ALUout), .in1(DataOut), .out(Ac_in_normal), .sel(LdA_from_MBR));
  Counter #(.width(24), .max('hffffff)) counter_1 (
    .load(controlunit_1_c2), .D(DataOut[23:0]), .count(controlunit_1_c1), .Q(counter_1_q), .clk(Clk),
    .clr(Reset));  // open: carry
  Register #(.width(24)) MAR (.D(multiplexer_1_out), .en(LoadMAR), .Q(Addr), .clk(Clk), .clr(Reset));
  Register #(.width(4)) IR (.D(DataOut[27:24]), .en(controlunit_1_c1), .clk(Clk), .clr(Reset));  // open: Q
  ControlUnit controlunit_1 (
    .IR(DataOut[27:24]), .Clk(Clk), .d1(d1), .c1(controlunit_1_c1), .R(R), .c2(controlunit_1_c2), .d2(d2),
    .b1(b1), .W(W), .increment_ac(controlunit_1_increment_ac), .decrement_ac(controlunit_1_decrement_ac),
    .LdAfrB(LdA_from_MBR), .Operation({c0, c1}), .LoadAc(LdA), .Reset(Reset), .mul_start(mul_start),
    .MUL_load(mul_load), .booth_done(booth_s_multiplier_1_done));
  Multiplexer #(.width(28), .enable("false")) multiplexer_3 (.in0(DataIn), .in1(Ac), .out(multiplexer_3_out), .sel(b1));
  or or_1 (or_1_out, controlunit_1_increment_ac, controlunit_1_decrement_ac);
  or or_2 (LoadMAR, d1, d2);
  Register #(.width(28)) MBR (.D(multiplexer_3_out), .en(LoadB), .Q(DataOut), .clk(Clk), .clr(Reset));
  Register #(.width(28)) u_Ac (.D(AcIn), .en(ac_enable), .Q(Ac), .clk(Clk), .clr(Reset));
  ALU_broad alu_broad_1 (
    .A(Ac), .B(multiplexer_4_out), .control0(c0), .control1(c1), .result(ALUout));  // open: zero, negative, overflow, carry
  Multiplexer #(.width(28), .enable("false")) multiplexer_4 (
    .in0(DataOut), .in1(28'h1), .out(multiplexer_4_out), .sel(or_1_out));
  or or_3 (LoadB, R, b1);
  or or_4 (LoadAc, LdA_from_MBR, LdA);
  Booth_s_multiplier booth_s_multiplier_1 (
    .M(Ac), .Q(DataOut), .Reset(Reset), .start(mul_start), .clock(Clk), .Done(booth_s_multiplier_1_done),
    .product_low(booth_s_multiplier_1_product_low));  // open: product_high
  or or_5 (ac_enable, LoadAc, mul_load);
  Multiplexer #(.width(28), .enable("false")) multiplexer_5 (
    .in0(Ac_in_normal), .in1(booth_s_multiplier_1_product_low), .out(AcIn), .sel(mul_load));

  // Other names for the same wires on the sheet: clr = Reset; MBRout[27:0] = DataOut
endmodule

// CU
module ControlUnit (
  input  [3:0] IR,
  input  Clk,
  input  Reset,
  input  booth_done,
  output d1,
  output c1,
  output R,
  output c2,
  output d2,
  output [1:0] Operation,
  output b1,
  output W,
  output increment_ac,
  output LoadAc,
  output decrement_ac,
  output LdAfrB,
  output mul_start,
  output MUL_load
);

  wire and_1_out, and_2_out, comparator_2_eq, decoder_1_out6, decoder_1_out7, decoder_1_out8, decoder_1_out9,
       decoder_1_out15, not_1_out, or_1_out, or_2_out, or_4_out, or_5_out;
  wire [5:0] counter_1_q;
  wire [6:0] rom_1_data;

  Counter #(.width(6), .max('h3f)) counter_1 (
    .load(rom_1_data[2]), .D({IR, 2'b11}), .count(or_5_out), .Q(counter_1_q), .clk(and_1_out), .clr(or_1_out));  // open: carry
  or or_1 (or_1_out, rom_1_data[1], Reset);
  and and_1 (and_1_out, Clk, not_1_out);
  ROM #(.addrWidth(6), .dataWidth(7)) rom_1 (.addr(counter_1_q), .data(rom_1_data));  // open: sel
  not not_1 (not_1_out, decoder_1_out15);
  Decoder #(.select(4), .enable("false")) decoder_1 (
    .out1(d1), .out2(c1), .out3(R), .out4(c2), .out5(d2), .out6(decoder_1_out6), .out7(decoder_1_out7),
    .out8(decoder_1_out8), .out9(decoder_1_out9), .out10(b1), .out11(W), .out12(increment_ac),
    .out13(decrement_ac), .out14(LdAfrB), .out15(decoder_1_out15), .sel(rom_1_data[6:3]));  // open: out0
  Comparator #(.width(6)) comparator_1 (.a(counter_1_q), .b(6'b101101), .eq(mul_start));  // open: gt, lt
  Comparator #(.width(6)) comparator_2 (.a(counter_1_q), .b(6'b101110), .eq(comparator_2_eq));  // open: gt, lt
  or or_2 (or_2_out, decoder_1_out7, increment_ac);
  or or_3 (LoadAc, decrement_ac, decoder_1_out6, or_2_out, decoder_1_out8, decoder_1_out9, increment_ac);
  and and_2 (and_2_out, booth_done, comparator_2_eq);
  or or_4 (or_4_out, decoder_1_out9, decrement_ac);
  or or_5 (or_5_out, and_2_out, rom_1_data[0]);
  Priority_Encoder #(.select(2)) priority_encoder_1 (
    .in0(decoder_1_out6), .in1(or_2_out), .in2(decoder_1_out8), .in3(or_4_out), .out(Operation));  // open: gs, en_out, en_in
  Comparator #(.width(6)) comparator_3 (.a(counter_1_q), .b(6'b101111), .eq(MUL_load));  // open: gt, lt

  // Notes on the sheet:
  //   contents of rom_1 (hex, n*v repeats v):
  //   9 19 14 29 19 31 2 29 19 39 2 29 51 59 2 29 19 41 2 29 19 49 2 21 2 2 2 29 19 71 2 78 0 0 0 61 2 0 0
  //   69 2 0 0 29 19 1 0 1 2
  //   mulwait
  //   wait advance
  //   counter count
endmodule
