// Logisim project Booths_multiplication28bit.circ as structural Verilog: 2 circuits, main circuit Booth's multiplier
module Booth_s_multiplier (
  input  [27:0] M,
  input  [27:0] Q,
  input  Reset,
  input  start,
  input  clock,
  output Done,
  output [27:0] product_high,
  output [27:0] product_low
);

  wire A_out, Busy_q, comparator_1_eq, controller_1_c0, controller_1_c1, controller_1_cl__a__q_1,
       controller_1_dec_cnt, controller_1_load__m__q__cnt, controller_1_load_a, controller_1_shr, not_1_out,
       or_1_out, or_2_out, Q_1_q0, Q_out;
  wire [4:0] counter_1_q;
  wire [27:0] alu_broad_1_result, M_q27;

  or or_1 (or_1_out, Reset, start);
  Register #(.width(1)) Busy (.D(not_1_out), .Q(Busy_q), .clk(clock), .clr(Reset));  // open: en
  Controller controller_1 (
    .Clk(clock), .Q0(product_low[0]), .Q_1(Q_1_q0), .Count(counter_1_q), .C0(controller_1_c0),
    .C1(controller_1_c1), .Shr(controller_1_shr), .Dec_Cnt(controller_1_dec_cnt),
    .Cl__A__Q_1(controller_1_cl__a__q_1), .Load_A(controller_1_load_a),
    .LOad__M__Q__Cnt(controller_1_load__m__q__cnt), .Reset(or_1_out));
  or or_2 (or_2_out, controller_1_load__m__q__cnt, controller_1_dec_cnt);
  Counter #(.width(5), .max('h1f)) counter_1 (
    .load(or_2_out), .D(5'b11100), .count(controller_1_dec_cnt), .Q(counter_1_q), .clk(clock));  // open: carry, clr
  Comparator #(.width(5)) comparator_1 (.a(counter_1_q), .b({5{1'b0}}), .eq(comparator_1_eq));  // open: gt, lt
  not not_1 (not_1_out, comparator_1_eq);
  and and_1 (Done, comparator_1_eq, Busy_q);
  Shift_Register #(.length(28)) u_M (
    .shift(1'b0), .clk(clock), .load(controller_1_load__m__q__cnt), .d0(M[27]), .q0(M_q27[27]), .d1(M[26]),
    .q1(M_q27[26]), .d2(M[25]), .q2(M_q27[25]), .d3(M[24]), .q3(M_q27[24]), .d4(M[23]), .q4(M_q27[23]),
    .d5(M[22]), .q5(M_q27[22]), .d6(M[21]), .q6(M_q27[21]), .d7(M[20]), .q7(M_q27[20]), .d8(M[19]),
    .q8(M_q27[19]), .d9(M[18]), .q9(M_q27[18]), .d10(M[17]), .q10(M_q27[17]), .d11(M[16]), .q11(M_q27[16]),
    .d12(M[15]), .q12(M_q27[15]), .d13(M[14]), .q13(M_q27[14]), .d14(M[13]), .q14(M_q27[13]), .d15(M[12]),
    .q15(M_q27[12]), .d16(M[11]), .q16(M_q27[11]), .d17(M[10]), .q17(M_q27[10]), .d18(M[9]), .q18(M_q27[9]),
    .d19(M[8]), .q19(M_q27[8]), .d20(M[7]), .q20(M_q27[7]), .d21(M[6]), .q21(M_q27[6]), .d22(M[5]),
    .q22(M_q27[5]), .d23(M[4]), .q23(M_q27[4]), .d24(M[3]), .q24(M_q27[3]), .d25(M[2]), .q25(M_q27[2]),
    .d26(M[1]), .q26(M_q27[1]), .d27(M[0]), .q27(M_q27[0]));  // open: in, out, clr
  Shift_Register #(.length(28)) A (
    .shift(controller_1_shr), .in(product_high[27]), .clk(clock), .out(A_out), .load(controller_1_load_a),
    .clr(controller_1_cl__a__q_1), .d0(alu_broad_1_result[27]), .q0(product_high[27]),
    .d1(alu_broad_1_result[26]), .q1(product_high[26]), .d2(alu_broad_1_result[25]), .q2(product_high[25]),
    .d3(alu_broad_1_result[24]), .q3(product_high[24]), .d4(alu_broad_1_result[23]), .q4(product_high[23]),
    .d5(alu_broad_1_result[22]), .q5(product_high[22]), .d6(alu_broad_1_result[21]), .q6(product_high[21]),
    .d7(alu_broad_1_result[20]), .q7(product_high[20]), .d8(alu_broad_1_result[19]), .q8(product_high[19]),
    .d9(alu_broad_1_result[18]), .q9(product_high[18]), .d10(alu_broad_1_result[17]), .q10(product_high[17]),
    .d11(alu_broad_1_result[16]), .q11(product_high[16]), .d12(alu_broad_1_result[15]),
    .q12(product_high[15]), .d13(alu_broad_1_result[14]), .q13(product_high[14]),
    .d14(alu_broad_1_result[13]), .q14(product_high[13]), .d15(alu_broad_1_result[12]),
    .q15(product_high[12]), .d16(alu_broad_1_result[11]), .q16(product_high[11]),
    .d17(alu_broad_1_result[10]), .q17(product_high[10]), .d18(alu_broad_1_result[9]), .q18(product_high[9]),
    .d19(alu_broad_1_result[8]), .q19(product_high[8]), .d20(alu_broad_1_result[7]), .q20(product_high[7]),
    .d21(alu_broad_1_result[6]), .q21(product_high[6]), .d22(alu_broad_1_result[5]), .q22(product_high[5]),
    .d23(alu_broad_1_result[4]), .q23(product_high[4]), .d24(alu_broad_1_result[3]), .q24(product_high[3]),
    .d25(alu_broad_1_result[2]), .q25(product_high[2]), .d26(alu_broad_1_result[1]), .q26(product_high[1]),
    .d27(alu_broad_1_result[0]), .q27(product_high[0]));
  ALU_broad alu_broad_1 (
    .A(product_high), .B(M_q27), .control0(controller_1_c0), .control1(controller_1_c1),
    .result(alu_broad_1_result));  // open: zero, negative, overflow, carry
  Shift_Register #(.length(28)) u_Q (
    .shift(controller_1_shr), .in(A_out), .clk(clock), .out(Q_out), .load(controller_1_load__m__q__cnt),
    .d0(Q[27]), .q0(product_low[27]), .d1(Q[26]), .q1(product_low[26]), .d2(Q[25]), .q2(product_low[25]),
    .d3(Q[24]), .q3(product_low[24]), .d4(Q[23]), .q4(product_low[23]), .d5(Q[22]), .q5(product_low[22]),
    .d6(Q[21]), .q6(product_low[21]), .d7(Q[20]), .q7(product_low[20]), .d8(Q[19]), .q8(product_low[19]),
    .d9(Q[18]), .q9(product_low[18]), .d10(Q[17]), .q10(product_low[17]), .d11(Q[16]), .q11(product_low[16]),
    .d12(Q[15]), .q12(product_low[15]), .d13(Q[14]), .q13(product_low[14]), .d14(Q[13]),
    .q14(product_low[13]), .d15(Q[12]), .q15(product_low[12]), .d16(Q[11]), .q16(product_low[11]),
    .d17(Q[10]), .q17(product_low[10]), .d18(Q[9]), .q18(product_low[9]), .d19(Q[8]), .q19(product_low[8]),
    .d20(Q[7]), .q20(product_low[7]), .d21(Q[6]), .q21(product_low[6]), .d22(Q[5]), .q22(product_low[5]),
    .d23(Q[4]), .q23(product_low[4]), .d24(Q[3]), .q24(product_low[3]), .d25(Q[2]), .q25(product_low[2]),
    .d26(Q[1]), .q26(product_low[1]), .d27(Q[0]), .q27(product_low[0]));  // open: clr
  Shift_Register #(.length(1)) Q_1 (
    .shift(controller_1_shr), .in(Q_out), .clk(clock), .clr(controller_1_cl__a__q_1), .q0(Q_1_q0));  // open: out, load, d0
endmodule

// Control \nUnit
module Controller (
  input  Clk,
  input  Reset,
  input  Q0,
  input  Q_1,
  input  [4:0] Count,
  output Cl__A__Q_1,
  output LOad__M__Q__Cnt,
  output Load_A,
  output C0,
  output C1,
  output Shr,
  output Dec_Cnt
);

  wire and_3_out, multiplexer_1_out, not_1_out, not_2_out, not_3_out, not_4_out, not_5_out, not_6_out,
       not_7_out, or_2_out, Q0_prime_Q_1_out, Q0Q_1_prime_out;
  wire [1:0] rom_1_data_2;
  wire [2:0] and_1_out, and_2_out, bit_extender_1_out, bit_extender_2_out, bit_extender_3_out, CAR_q,
       or_1_out, rom_1_data;

  assign bit_extender_1_out = {{2{Q0_prime_Q_1_out}}, Q0_prime_Q_1_out};  // Bit_Extender bit_extender_1
  and Q0_prime_Q_1 (Q0_prime_Q_1_out, not_2_out, Q_1);
  not not_1 (not_1_out, Q0_prime_Q_1_out);
  assign bit_extender_2_out = {{2{not_1_out}}, not_1_out};  // Bit_Extender bit_extender_2
  assign and_1_out = 3'b100 & bit_extender_3_out & bit_extender_1_out;  // AND_Gate and_1, 3 bits wide
  assign or_1_out = and_1_out | rom_1_data | and_2_out;  // OR_Gate or_1, 3 bits wide
  not not_2 (not_2_out, Q0);
  assign and_2_out = bit_extender_2_out & bit_extender_3_out & 3'b101;  // AND_Gate and_2, 3 bits wide
  assign bit_extender_3_out = {{2{and_3_out}}, and_3_out};  // Bit_Extender bit_extender_3
  and and_3 (and_3_out, not_4_out, CAR_q[1], not_3_out);
  not not_3 (not_3_out, CAR_q[0]);
  not not_4 (not_4_out, CAR_q[2]);
  Counter #(.width(3), .max('h7)) CAR (
    .load(not_5_out), .D(or_1_out), .count(multiplexer_1_out), .Q(CAR_q), .clk(Clk), .clr(Reset));  // open: carry
  not not_5 (not_5_out, multiplexer_1_out);
  Multiplexer #(.select(2), .enable("false")) multiplexer_1 (
    .in0(1'b0), .in1(1'b1), .in2(Q0Q_1_prime_out), .in3(not_7_out), .out(multiplexer_1_out),
    .sel(rom_1_data_2));
  ROM #(.addrWidth(3), .dataWidth(12)) rom_1 (
    .addr(CAR_q), .data({Cl__A__Q_1, LOad__M__Q__Cnt, Load_A, C0, C1, Shr, Dec_Cnt, rom_1_data, rom_1_data_2}));  // open: sel
  and Q0Q_1_prime (Q0Q_1_prime_out, not_6_out, Q0);
  not not_6 (not_6_out, Q_1);
  or or_2 (or_2_out, Count[0], Count[1], Count[2], Count[3], Count[4]);
  not not_7 (not_7_out, or_2_out);

  // Notes on the sheet:
  //   To choose only
  //   state 2 (010)
  //   Control Word Format: Clear (A, Q-1), Load (M, Q, Cnt), Load A, C0, C1, Shr, Dec Cnt, Address bits (3 bit), Selection bits (2 bit)
  //   contents of rom_1 (hex, n*v repeats v):
  //   1 c01 2 394 281 61 b 1c
endmodule
